# Fritzing sketch dice_v1 (saved by Fritzing 0.8.7b)
circuit board: 11.9523cm x 5.8086cm
breadboards: 3

parts:
  Display_1 = 7-SEGMENT-DISPLAY-1_-RED [package=7-segment-1_pth]
  Shift_2 = 74HC595 [package="DIP16 [THT]"]
  Display_2 = 7-SEGMENT-DISPLAY-1_-RED [package=7-segment-1_pth]
  R2 = Resistor [tolerance=±5% resistance=220 package=THT]
  R1 = Resistor [tolerance=±5% resistance=220 package=THT]
  S1 = Pushbutton [package="[THT]"]
  R3 = Resistor [tolerance=±5% resistance=22k package=THT]
  LED1 = LED - 5mm [color="Blue (505nm)" package="5 mm [THT]"]
  S2 = Pushbutton [package="[THT]"]
  R4 = Resistor [tolerance=±5% resistance=22k package=THT]
  LED2 = LED - 5mm [color="Blue (505nm)" package="5 mm [THT]"]
  S3 = Pushbutton [package="[THT]"]
  R5 = Resistor [tolerance=±5% resistance=22k package=THT]
  LED3 = LED - 5mm [color="Blue (505nm)" package="5 mm [THT]"]
  S4 = Pushbutton [package="[THT]"]
  R6 = Resistor [tolerance=±5% resistance=22k package=THT]
  LED4 = LED - 5mm [color="Blue (505nm)" package="5 mm [THT]"]
  S5 = Pushbutton [package="[THT]"]
  R7 = Resistor [tolerance=±5% resistance=22k package=THT]
  LED5 = LED - 5mm [color="Blue (505nm)" package="5 mm [THT]"]
  S6 = Pushbutton [package="[THT]"]
  R8 = Resistor [tolerance=±5% resistance=22k package=THT]
  LED6 = LED - 5mm [color="Blue (505nm)" package="5 mm [THT]"]
  S7 = Pushbutton [package="[THT]"]
  R9 = Resistor [tolerance=±5% resistance=22k package=THT]
  LED7 = LED - 5mm [color="Blue (505nm)" package="5 mm [THT]"]
  Registers = female pin header, 3 pins [form="♀ (female)"]
  Power = female pin header, 2 pins [form="♀ (female)"]
  Switches = female pin header, 7 pins [form="♀ (female)"]
  Shift_1 = 74HC595 [package="DIP16 [THT]"]

nets:
  N1: Display_1.E, Shift_1.Q4
  N2: Display_1.D, Shift_1.Q3
  N3: Display_1.G1, R1.Pin_1
  N4: Display_1.C, Shift_1.Q2
  N5: Display_1.DP, Shift_1.Q7
  N6: Display_1.B, Shift_1.Q1
  N7: Display_1.A, Shift_1.Q0
  N8: Display_1.F, Shift_1.Q5
  N9: Display_1.G, Shift_1.Q6
  N10: Shift_2.Q1, Display_2.B
  N11: Shift_2.Q2, Display_2.C
  N12: Shift_2.Q3, Display_2.D
  N13: Shift_2.Q4, Display_2.E
  N14: Shift_2.Q5, Display_2.F
  N15: Shift_2.Q6, Display_2.G
  N16: Shift_2.Q7, Display_2.DP
  GND: Shift_2.GND, Shift_2.OE, LED1.cathode, LED2.cathode, LED3.cathode, LED4.cathode, LED5.cathode, LED6.cathode, LED7.cathode, Power.pin1, Shift_1.GND, Shift_1.OE
  VCC: Shift_2.MR, Shift_2.VCC, R2.Pin_0, R1.Pin_0, S1.Pin_1, S1.Pin_2, S2.Pin_1, S2.Pin_2, S3.Pin_1, S3.Pin_2, S4.Pin_1, S4.Pin_2, S5.Pin_1, S5.Pin_2, S6.Pin_1, S6.Pin_2, S7.Pin_1, S7.Pin_2, Power.pin2, Shift_1.MR, Shift_1.VCC
  N17: Shift_2.SH_CP, Registers.pin1, Shift_1.SH_CP
  N18: Shift_2.ST_CP, Registers.pin3, Shift_1.ST_CP
  N19: Shift_2.DS, Shift_1.Q7'
  N20: Shift_2.Q0, Display_2.A
  N21: Display_2.G1, R2.Pin_1
  N22: S1.Pin_3, S1.Pin_4, R3.Pin_1, Switches.pin1
  N23: R3.Pin_0, LED1.anode
  N24: S2.Pin_3, S2.Pin_4, R4.Pin_1, Switches.pin2
  N25: R4.Pin_0, LED2.anode
  N26: S3.Pin_3, S3.Pin_4, R5.Pin_1, Switches.pin3
  N27: R5.Pin_0, LED3.anode
  N28: S4.Pin_3, S4.Pin_4, R6.Pin_1, Switches.pin4
  N29: R6.Pin_0, LED4.anode
  N30: S5.Pin_3, S5.Pin_4, R7.Pin_1, Switches.pin5
  N31: R7.Pin_0, LED5.anode
  N32: S6.Pin_3, S6.Pin_4, R8.Pin_1, Switches.pin6
  N33: R8.Pin_0, LED6.anode
  N34: S7.Pin_3, S7.Pin_4, R9.Pin_1, Switches.pin7
  N35: R9.Pin_0, LED7.anode
  N36: Registers.pin2, Shift_1.DS

notes:
  Dungeon Dice, Digital d4 - d100 roller using an Arduino, 1
  Dice Roller V1
  GND
  5V
  CLOCK
  DATA
  LATCH
  d10
  d12
  d8
  d6
  d4
  d100
  d20
  pissedoffadmins.com
