# Fritzing sketch dice_v2 (saved by Fritzing 0.8.7b)
circuit board: 7.51738cm x 7.54039cm
breadboards: 2

parts:
  Atmega328 = atmega328 [package=dip]
  R8 = Resistor [tolerance=±5% resistance=22k package=THT]
  LED2 = LED - 5mm [color="Blue (505nm)" package="5 mm [THT]"]
  C2 = Ceramic Capacitor [capacitance=22pF package="100 mil [THT, multilayer]"]
  R1 = Resistor [tolerance=±5% resistance=220 package=THT]
  S7 = Pushbutton [package="[THT]"]
  Shift_1 = 74HC595 [package="DIP16 [THT]"]
  R2 = Resistor [tolerance=±5% resistance=220 package=THT]
  R9 = Resistor [tolerance=±5% resistance=22k package=THT]
  R3 = Resistor [tolerance=±5% resistance=22k package=THT]
  LED8 = LED - 5mm [color="Blue (505nm)" package="5 mm [THT]"]
  LED7 = LED - 5mm [color="Blue (505nm)" package="5 mm [THT]"]
  LED5 = LED - 5mm [color="Blue (505nm)" package="5 mm [THT]"]
  C1 = Ceramic Capacitor [capacitance=22pF package="100 mil [THT, multilayer]"]
  S2 = Pushbutton [package="[THT]"]
  XTAL1 = Crystal [frequency="16 MHz" package=THT]
  S6 = Pushbutton [package="[THT]"]
  S4 = Pushbutton [package="[THT]"]
  R4 = Resistor [tolerance=±5% resistance=22k package=THT]
  R11 = Resistor [tolerance=±5% resistance=220 package=THT]
  LED3 = LED - 5mm [color="Blue (505nm)" package="5 mm [THT]"]
  LED4 = LED - 5mm [color="Blue (505nm)" package="5 mm [THT]"]
  Display_2 = 7-SEGMENT-DISPLAY-1_-RED [package=7-segment-1_pth]
  R5 = Resistor [tolerance=±5% resistance=22k package=THT]
  Shift_2 = 74HC595 [package="DIP16 [THT]"]
  S3 = Pushbutton [package="[THT]"]
  S5 = Pushbutton [package="[THT]"]
  R10 = Resistor [tolerance=±5% resistance=10k package=THT]
  R7 = Resistor [tolerance=±5% resistance=22k package=THT]
  R6 = Resistor [tolerance=±5% resistance=22k package=THT]
  LED1 = LED - 5mm [color="Blue (505nm)" package="5 mm [THT]"]
  LED6 = LED - 5mm [color="Blue (505nm)" package="5 mm [THT]"]
  S1 = Pushbutton [package="[THT]"]
  S8 = Pushbutton [package=THT]
  Display_1 = 7-SEGMENT-DISPLAY-1_-RED [package=7-segment-1_pth]
  VCC1 = Battery

nets (from the schematic view):
  N1: Atmega328.RESET, R10.Pin_1, S8.leg0
  N2: Atmega328.D2, Shift_1.ST_CP, Shift_2.ST_CP
  N3: Atmega328.D3_(PWM), Shift_1.DS
  N4: Atmega328.D4, Shift_1.SH_CP, Shift_2.SH_CP
  VCC: Atmega328.VCC, Atmega328.AVCC, Atmega328.AREF, R1.Pin_0, S7.Pin_1, S7.Pin_2, Shift_1.MR, Shift_1.VCC, R2.Pin_0, S2.Pin_1, S2.Pin_2, S6.Pin_1, S6.Pin_2, S4.Pin_1, S4.Pin_2, Shift_2.MR, Shift_2.VCC, S3.Pin_1, S3.Pin_2, S5.Pin_1, S5.Pin_2, R10.Pin_0, S1.Pin_1, S1.Pin_2, VCC1.-
  GND: Atmega328.GND, LED2.cathode, C2.0, Shift_1.GND, Shift_1.OE, LED7.cathode, LED5.cathode, C1.0, R11.Pin_0, LED3.cathode, LED4.cathode, Shift_2.GND, Shift_2.OE, LED1.cathode, LED6.cathode, S8.leg1, VCC1.+
  N5: Atmega328.XLAT1, C1.1, XTAL1.pin_1
  N6: Atmega328.XLAT2, C2.1, XTAL1.pin_0
  N7: Atmega328.D6_(PWM), S7.Pin_3, S7.Pin_4, R9.Pin_1
  N8: Atmega328.D7, R8.Pin_1, S6.Pin_3, S6.Pin_4
  N9: Atmega328.D8, S5.Pin_3, S5.Pin_4, R7.Pin_1
  N10: Atmega328.D9_(PWM), S4.Pin_3, S4.Pin_4, R6.Pin_1
  N11: Atmega328.D10_(PWM), R5.Pin_1, S3.Pin_3, S3.Pin_4
  N12: Atmega328.D11_(PWM), S2.Pin_3, S2.Pin_4, R4.Pin_1
  N13: Atmega328.D12, R3.Pin_1, S1.Pin_3, S1.Pin_4
  N14: Atmega328.D13, LED8.anode
  N15: R8.Pin_0, LED6.anode
  N16: LED2.anode, R4.Pin_0
  N17: R1.Pin_1, Display_1.G1
  N18: Shift_1.Q1, Display_1.B
  N19: Shift_1.Q2, Display_1.C
  N20: Shift_1.Q3, Display_1.D
  N21: Shift_1.Q4, Display_1.E
  N22: Shift_1.Q5, Display_1.F
  N23: Shift_1.Q6, Display_1.G
  N24: Shift_1.Q7, Display_1.DP
  N25: Shift_1.Q7', Shift_2.DS
  N26: Shift_1.Q0, Display_1.A
  N27: R2.Pin_1, Display_2.G1
  N28: R9.Pin_0, LED7.anode
  N29: R3.Pin_0, LED1.anode
  N30: LED8.cathode, R11.Pin_1
  N31: LED5.anode, R7.Pin_0
  N32: LED3.anode, R5.Pin_0
  N33: LED4.anode, R6.Pin_0
  N34: Display_2.E, Shift_2.Q4
  N35: Display_2.D, Shift_2.Q3
  N36: Display_2.C, Shift_2.Q2
  N37: Display_2.DP, Shift_2.Q7
  N38: Display_2.B, Shift_2.Q1
  N39: Display_2.A, Shift_2.Q0
  N40: Display_2.F, Shift_2.Q5
  N41: Display_2.G, Shift_2.Q6

notes:
  d4
  d6
  d8
  d10
  d12
  d20
  d100
  Dice Roller V2
  pissedoffadmins.com
  Digital d4 - d100 roller using an Arduino, 2
